# Fritzing sketch Lunar (saved by Fritzing 0.9.3b)

parts:
  Nano = Arduino Nano (Rev3.0)
  R1 = Resistor [tolerance=±5% resistance=1k package=THT]
  SPST = SWITCH_SPDT [package=kps-1290]
  DS3231 = DS1307 RTC Breakout
  JP1 = Header 6 [package=1x06_smd_straight_alt]
  JP2 = Header 1 [package=1x01_offset]
  JP3 = Header 1 [package=1x01_offset]
  JP4 = Header 1 [package=1x01_offset]
  C1 = Electrolytic Capacitor [capacitance=0.01mF voltage=15V package="300 mil [THT, electrolytic]"]
  J1 = Basic Servo  # not connected
  J2 = Dagu DGServo 9g header (male) [package=THT]  # not connected
  J3 = Dagu DGServo 9g header (male) [package=THT]
  J4 = Dagu DGServo 9g header (male) [package=THT]
  M1 = DC Motor
  U2 = mystery part, 3 pins [chip_label=?]
  U3 = mystery part, 3 pins [chip_label=?]
  C2 = Ceramic Capacitor [capacitance="100 nF" package="0805 [SMD, multilayer]"]
  HC05 = Bluetooth HC-05 Macho
  R2 = Resistor [tolerance=±5% resistance=220 package=THT]

nets:
  N1: Nano.D1/TX, R1.Pin_0
  N2: Nano.D0/RX, HC05.TXD
  N3: Nano.D4, JP3.1
  N4: Nano.D11/MOSI, JP1.5
  N5: Nano.D12/MISO, JP1.6
  GND: Nano.GND, DS3231.GND
  N6: Nano.A5, DS3231.SCL
  N7: Nano.A4, DS3231.SDA
  N8: Nano.A2, JP1.1
  N9: Nano.A1, JP1.2
  N10: SPST.O, HC05.VCC
  N11: JP2.1, C1.+
  N12: JP4.1, C1.-, HC05.GND, R2.Pin_1
  N13: J3.gnd, U3.pin3
  N14: J3.Vcc, U2.pin3
  N15: J3.pulse, U2.pin1
  N16: J4.gnd, U2.pin2
  N17: J4.Vcc, M1.pin_1, C2.1
  N18: J4.pulse, M1.pin_2, C2.0
  N19: HC05.RXD, R2.Pin_0

notes:
  A1302KUA-T   Hall Sensors
  Planetary Gearmotor, 1014:1 ratio  GMP16D1014
  Switch off Bluetooth to program

custom parts:
  DS1307 RTC Breakout: DS1307 Real-time Clock Breakout Board with Battery
